// Digital circuit Memory 1B.dig as structural Verilog
module Memory_1B (
  input  I0,
  input  I1,
  input  I2,
  input  I3,
  input  I4,
  input  I5,
  input  I6,
  input  I7,
  input  RESET,
  input  SET,
  output O0,
  output O1,
  output O2,
  output O3,
  output O4,
  output O5,
  output O6,
  output O7
);

  wire and_1_out, and_2_out, and_3_out, and_4_out, and_5_out, and_6_out, and_7_out, and_8_out, nor_1_out,
       nor_3_out, nor_5_out, nor_7_out, nor_9_out, nor_11_out, nor_13_out, nor_15_out;

  and and_1 (and_1_out, SET, I7);
  and and_2 (and_2_out, SET, I6);
  and and_3 (and_3_out, SET, I5);
  and and_4 (and_4_out, SET, I4);
  and and_5 (and_5_out, SET, I3);
  and and_6 (and_6_out, SET, I2);
  and and_7 (and_7_out, SET, I1);
  and and_8 (and_8_out, SET, I0);
  nor nor_1 (nor_1_out, and_1_out, O7);
  nor nor_2 (O7, nor_1_out, RESET);
  nor nor_3 (nor_3_out, and_2_out, O6);
  nor nor_4 (O6, nor_3_out, RESET);
  nor nor_5 (nor_5_out, and_3_out, O5);
  nor nor_6 (O5, nor_5_out, RESET);
  nor nor_7 (nor_7_out, and_4_out, O4);
  nor nor_8 (O4, nor_7_out, RESET);
  nor nor_9 (nor_9_out, and_5_out, O3);
  nor nor_10 (O3, nor_9_out, RESET);
  nor nor_11 (nor_11_out, and_6_out, O2);
  nor nor_12 (O2, nor_11_out, RESET);
  nor nor_13 (nor_13_out, and_7_out, O1);
  nor nor_14 (O1, nor_13_out, RESET);
  nor nor_15 (nor_15_out, and_8_out, O0);
  nor nor_16 (O0, nor_15_out, RESET);
endmodule
