// Digital circuit Memory 4R8b.dig as structural Verilog
module Memory_4R8b (
  input  I0,
  input  I1,
  input  I2,
  input  I3,
  input  I4,
  input  I5,
  input  I6,
  input  I7,
  input  R0,
  input  S0,
  input  R1,
  input  S1,
  input  R2,
  input  S2,
  input  R3,
  input  S3,
  output O00,
  output O01,
  output O02,
  output O03,
  output O04,
  output O05,
  output O06,
  output O07,
  output O10,
  output O11,
  output O12,
  output O13,
  output O14,
  output O15,
  output O16,
  output O17,
  output O20,
  output O21,
  output O22,
  output O23,
  output O24,
  output O25,
  output O26,
  output O27,
  output O30,
  output O31,
  output O32,
  output O33,
  output O34,
  output O35,
  output O36,
  output O37
);

  wire and_1_out, and_2_out, and_3_out, and_4_out, and_5_out, and_6_out, and_7_out, and_8_out, and_9_out,
       and_10_out, and_11_out, and_12_out, and_13_out, and_14_out, and_15_out, and_16_out, and_17_out,
       and_18_out, and_19_out, and_20_out, and_21_out, and_22_out, and_23_out, and_24_out, and_25_out,
       and_26_out, and_27_out, and_28_out, and_29_out, and_30_out, and_31_out, and_32_out, nor_1_out,
       nor_3_out, nor_5_out, nor_7_out, nor_9_out, nor_11_out, nor_13_out, nor_15_out, nor_17_out,
       nor_19_out, nor_21_out, nor_23_out, nor_25_out, nor_27_out, nor_29_out, nor_31_out, nor_33_out,
       nor_35_out, nor_37_out, nor_39_out, nor_41_out, nor_43_out, nor_45_out, nor_47_out, nor_49_out,
       nor_51_out, nor_53_out, nor_55_out, nor_57_out, nor_59_out, nor_61_out, nor_63_out;

  and and_1 (and_1_out, S0, I7);
  and and_2 (and_2_out, S0, I6);
  and and_3 (and_3_out, S0, I5);
  and and_4 (and_4_out, S0, I4);
  and and_5 (and_5_out, S0, I3);
  and and_6 (and_6_out, S0, I2);
  and and_7 (and_7_out, S0, I1);
  and and_8 (and_8_out, S0, I0);
  nor nor_1 (nor_1_out, and_1_out, O07);
  nor nor_2 (O07, nor_1_out, R0);
  nor nor_3 (nor_3_out, and_2_out, O06);
  nor nor_4 (O06, nor_3_out, R0);
  nor nor_5 (nor_5_out, and_3_out, O05);
  nor nor_6 (O05, nor_5_out, R0);
  nor nor_7 (nor_7_out, and_4_out, O04);
  nor nor_8 (O04, nor_7_out, R0);
  nor nor_9 (nor_9_out, and_5_out, O03);
  nor nor_10 (O03, nor_9_out, R0);
  nor nor_11 (nor_11_out, and_6_out, O02);
  nor nor_12 (O02, nor_11_out, R0);
  nor nor_13 (nor_13_out, and_7_out, O01);
  nor nor_14 (O01, nor_13_out, R0);
  nor nor_15 (nor_15_out, and_8_out, O00);
  nor nor_16 (O00, nor_15_out, R0);
  and and_9 (and_9_out, S1, I7);
  and and_10 (and_10_out, S1, I6);
  and and_11 (and_11_out, S1, I5);
  and and_12 (and_12_out, S1, I4);
  and and_13 (and_13_out, S1, I3);
  and and_14 (and_14_out, S1, I2);
  and and_15 (and_15_out, S1, I1);
  and and_16 (and_16_out, S1, I0);
  nor nor_17 (nor_17_out, and_9_out, O17);
  nor nor_18 (O17, nor_17_out, R1);
  nor nor_19 (nor_19_out, and_10_out, O16);
  nor nor_20 (O16, nor_19_out, R1);
  nor nor_21 (nor_21_out, and_11_out, O15);
  nor nor_22 (O15, nor_21_out, R1);
  nor nor_23 (nor_23_out, and_12_out, O14);
  nor nor_24 (O14, nor_23_out, R1);
  nor nor_25 (nor_25_out, and_13_out, O13);
  nor nor_26 (O13, nor_25_out, R1);
  nor nor_27 (nor_27_out, and_14_out, O12);
  nor nor_28 (O12, nor_27_out, R1);
  nor nor_29 (nor_29_out, and_15_out, O11);
  nor nor_30 (O11, nor_29_out, R1);
  nor nor_31 (nor_31_out, and_16_out, O10);
  nor nor_32 (O10, nor_31_out, R1);
  and and_17 (and_17_out, S2, I7);
  and and_18 (and_18_out, S2, I6);
  and and_19 (and_19_out, S2, I5);
  and and_20 (and_20_out, S2, I4);
  and and_21 (and_21_out, S2, I3);
  and and_22 (and_22_out, S2, I2);
  and and_23 (and_23_out, S2, I1);
  and and_24 (and_24_out, S2, I0);
  nor nor_33 (nor_33_out, and_17_out, O27);
  nor nor_34 (O27, nor_33_out, R2);
  nor nor_35 (nor_35_out, and_18_out, O26);
  nor nor_36 (O26, nor_35_out, R2);
  nor nor_37 (nor_37_out, and_19_out, O25);
  nor nor_38 (O25, nor_37_out, R2);
  nor nor_39 (nor_39_out, and_20_out, O24);
  nor nor_40 (O24, nor_39_out, R2);
  nor nor_41 (nor_41_out, and_21_out, O23);
  nor nor_42 (O23, nor_41_out, R2);
  nor nor_43 (nor_43_out, and_22_out, O22);
  nor nor_44 (O22, nor_43_out, R2);
  nor nor_45 (nor_45_out, and_23_out, O21);
  nor nor_46 (O21, nor_45_out, R2);
  nor nor_47 (nor_47_out, and_24_out, O20);
  nor nor_48 (O20, nor_47_out, R2);
  and and_25 (and_25_out, S3, I7);
  and and_26 (and_26_out, S3, I6);
  and and_27 (and_27_out, S3, I5);
  and and_28 (and_28_out, S3, I4);
  and and_29 (and_29_out, S3, I3);
  and and_30 (and_30_out, S3, I2);
  and and_31 (and_31_out, S3, I1);
  and and_32 (and_32_out, S3, I0);
  nor nor_49 (nor_49_out, and_25_out, O37);
  nor nor_50 (O37, nor_49_out, R3);
  nor nor_51 (nor_51_out, and_26_out, O36);
  nor nor_52 (O36, nor_51_out, R3);
  nor nor_53 (nor_53_out, and_27_out, O35);
  nor nor_54 (O35, nor_53_out, R3);
  nor nor_55 (nor_55_out, and_28_out, O34);
  nor nor_56 (O34, nor_55_out, R3);
  nor nor_57 (nor_57_out, and_29_out, O33);
  nor nor_58 (O33, nor_57_out, R3);
  nor nor_59 (nor_59_out, and_30_out, O32);
  nor nor_60 (O32, nor_59_out, R3);
  nor nor_61 (nor_61_out, and_31_out, O31);
  nor nor_62 (O31, nor_61_out, R3);
  nor nor_63 (nor_63_out, and_32_out, O30);
  nor nor_64 (O30, nor_63_out, R3);

  // Notes on the sheet:
  //   Memory
endmodule
