// Digital circuit computer.dig as structural Verilog
module computer (
  input  I0,
  input  I1,
  input  I2,
  input  I3,
  input  I4,
  input  I5,
  input  I6,
  input  I7
);

  wire and_1_out, and_2_out, and_3_out, and_4_out, and_5_out, and_6_out, and_7_out, and_8_out, and_9_out,
       and_10_out, and_11_out, and_12_out, and_13_out, and_14_out, and_15_out, and_16_out, and_17_out,
       and_18_out, and_19_out, and_20_out, and_21_out, and_22_out, and_23_out, and_24_out, and_25_out,
       and_26_out, and_27_out, and_28_out, and_29_out, and_30_out, and_31_out, and_32_out, nor_1_out,
       nor_2_out, nor_3_out, nor_4_out, nor_5_out, nor_6_out, nor_7_out, nor_8_out, nor_9_out, nor_10_out,
       nor_11_out, nor_12_out, nor_13_out, nor_14_out, nor_15_out, nor_16_out, nor_17_out, nor_18_out,
       nor_19_out, nor_20_out, nor_21_out, nor_22_out, nor_23_out, nor_24_out, nor_25_out, nor_26_out,
       nor_27_out, nor_28_out, nor_29_out, nor_30_out, nor_31_out, nor_32_out, nor_33_out, nor_34_out,
       nor_35_out, nor_36_out, nor_37_out, nor_38_out, nor_39_out, nor_40_out, nor_41_out, nor_42_out,
       nor_43_out, nor_44_out, nor_45_out, nor_46_out, nor_47_out, nor_48_out, nor_49_out, nor_50_out,
       nor_51_out, nor_52_out, nor_53_out, nor_54_out, nor_55_out, nor_56_out, nor_57_out, nor_58_out,
       nor_59_out, nor_60_out, nor_61_out, nor_62_out, nor_63_out, nor_64_out, RESET_2_out, RESET_3_out,
       RESET_4_out, RESET_out, SET_2_out, SET_3_out, SET_4_out, SET_out;

  Button SET (.out(SET_out));
  Button RESET (.out(RESET_out));
  and and_1 (and_1_out, I0, SET_out);
  and and_2 (and_2_out, I1, SET_out);
  and and_3 (and_3_out, I2, SET_out);
  and and_4 (and_4_out, I3, SET_out);
  and and_5 (and_5_out, I4, SET_out);
  and and_6 (and_6_out, I5, SET_out);
  and and_7 (and_7_out, I6, SET_out);
  and and_8 (and_8_out, I7, SET_out);
  nor nor_1 (nor_1_out, and_1_out, nor_2_out);
  nor nor_2 (nor_2_out, nor_1_out, RESET_out);
  nor nor_3 (nor_3_out, and_2_out, nor_4_out);
  nor nor_4 (nor_4_out, nor_3_out, RESET_out);
  nor nor_5 (nor_5_out, and_3_out, nor_6_out);
  nor nor_6 (nor_6_out, nor_5_out, RESET_out);
  nor nor_7 (nor_7_out, and_4_out, nor_8_out);
  nor nor_8 (nor_8_out, nor_7_out, RESET_out);
  nor nor_9 (nor_9_out, and_5_out, nor_10_out);
  nor nor_10 (nor_10_out, nor_9_out, RESET_out);
  nor nor_11 (nor_11_out, and_6_out, nor_12_out);
  nor nor_12 (nor_12_out, nor_11_out, RESET_out);
  nor nor_13 (nor_13_out, and_7_out, nor_14_out);
  nor nor_14 (nor_14_out, nor_13_out, RESET_out);
  nor nor_15 (nor_15_out, and_8_out, nor_16_out);
  nor nor_16 (nor_16_out, nor_15_out, RESET_out);
  Button SET_2 (.out(SET_2_out));
  Button RESET_2 (.out(RESET_2_out));
  and and_9 (and_9_out, I0, SET_2_out);
  and and_10 (and_10_out, I1, SET_2_out);
  and and_11 (and_11_out, I2, SET_2_out);
  and and_12 (and_12_out, I3, SET_2_out);
  and and_13 (and_13_out, I4, SET_2_out);
  and and_14 (and_14_out, I5, SET_2_out);
  and and_15 (and_15_out, I6, SET_2_out);
  and and_16 (and_16_out, I7, SET_2_out);
  nor nor_17 (nor_17_out, and_9_out, nor_18_out);
  nor nor_18 (nor_18_out, nor_17_out, RESET_2_out);
  nor nor_19 (nor_19_out, and_10_out, nor_20_out);
  nor nor_20 (nor_20_out, nor_19_out, RESET_2_out);
  nor nor_21 (nor_21_out, and_11_out, nor_22_out);
  nor nor_22 (nor_22_out, nor_21_out, RESET_2_out);
  nor nor_23 (nor_23_out, and_12_out, nor_24_out);
  nor nor_24 (nor_24_out, nor_23_out, RESET_2_out);
  nor nor_25 (nor_25_out, and_13_out, nor_26_out);
  nor nor_26 (nor_26_out, nor_25_out, RESET_2_out);
  nor nor_27 (nor_27_out, and_14_out, nor_28_out);
  nor nor_28 (nor_28_out, nor_27_out, RESET_2_out);
  nor nor_29 (nor_29_out, and_15_out, nor_30_out);
  nor nor_30 (nor_30_out, nor_29_out, RESET_2_out);
  nor nor_31 (nor_31_out, and_16_out, nor_32_out);
  nor nor_32 (nor_32_out, nor_31_out, RESET_2_out);
  Button SET_3 (.out(SET_3_out));
  Button RESET_3 (.out(RESET_3_out));
  and and_17 (and_17_out, I0, SET_3_out);
  and and_18 (and_18_out, I1, SET_3_out);
  and and_19 (and_19_out, I2, SET_3_out);
  and and_20 (and_20_out, I3, SET_3_out);
  and and_21 (and_21_out, I4, SET_3_out);
  and and_22 (and_22_out, I5, SET_3_out);
  and and_23 (and_23_out, I6, SET_3_out);
  and and_24 (and_24_out, I7, SET_3_out);
  nor nor_33 (nor_33_out, and_17_out, nor_34_out);
  nor nor_34 (nor_34_out, nor_33_out, RESET_3_out);
  nor nor_35 (nor_35_out, and_18_out, nor_36_out);
  nor nor_36 (nor_36_out, nor_35_out, RESET_3_out);
  nor nor_37 (nor_37_out, and_19_out, nor_38_out);
  nor nor_38 (nor_38_out, nor_37_out, RESET_3_out);
  nor nor_39 (nor_39_out, and_20_out, nor_40_out);
  nor nor_40 (nor_40_out, nor_39_out, RESET_3_out);
  nor nor_41 (nor_41_out, and_21_out, nor_42_out);
  nor nor_42 (nor_42_out, nor_41_out, RESET_3_out);
  nor nor_43 (nor_43_out, and_22_out, nor_44_out);
  nor nor_44 (nor_44_out, nor_43_out, RESET_3_out);
  nor nor_45 (nor_45_out, and_23_out, nor_46_out);
  nor nor_46 (nor_46_out, nor_45_out, RESET_3_out);
  nor nor_47 (nor_47_out, and_24_out, nor_48_out);
  nor nor_48 (nor_48_out, nor_47_out, RESET_3_out);
  Button SET_4 (.out(SET_4_out));
  Button RESET_4 (.out(RESET_4_out));
  and and_25 (and_25_out, I0, SET_4_out);
  and and_26 (and_26_out, I1, SET_4_out);
  and and_27 (and_27_out, I2, SET_4_out);
  and and_28 (and_28_out, I3, SET_4_out);
  and and_29 (and_29_out, I4, SET_4_out);
  and and_30 (and_30_out, I5, SET_4_out);
  and and_31 (and_31_out, I6, SET_4_out);
  and and_32 (and_32_out, I7, SET_4_out);
  nor nor_49 (nor_49_out, and_25_out, nor_50_out);
  nor nor_50 (nor_50_out, nor_49_out, RESET_4_out);
  nor nor_51 (nor_51_out, and_26_out, nor_52_out);
  nor nor_52 (nor_52_out, nor_51_out, RESET_4_out);
  nor nor_53 (nor_53_out, and_27_out, nor_54_out);
  nor nor_54 (nor_54_out, nor_53_out, RESET_4_out);
  nor nor_55 (nor_55_out, and_28_out, nor_56_out);
  nor nor_56 (nor_56_out, nor_55_out, RESET_4_out);
  nor nor_57 (nor_57_out, and_29_out, nor_58_out);
  nor nor_58 (nor_58_out, nor_57_out, RESET_4_out);
  nor nor_59 (nor_59_out, and_30_out, nor_60_out);
  nor nor_60 (nor_60_out, nor_59_out, RESET_4_out);
  nor nor_61 (nor_61_out, and_31_out, nor_62_out);
  nor nor_62 (nor_62_out, nor_61_out, RESET_4_out);
  nor nor_63 (nor_63_out, and_32_out, nor_64_out);
  nor nor_64 (nor_64_out, nor_63_out, RESET_4_out);

  // Notes on the sheet:
  //   Register 0
  //   Register 1
  //   Memory
  //   Register 2
  //   Register 3
endmodule
